# Fritzing sketch Diagram (saved by Fritzing 0.9.3b)
breadboards: 1

parts:
  SparkFun_Load_Cell_Amplifier_-_HX1 = SparkFun Load Cell Amplifier - HX711 [part_number=SEN-13879]
  Part1 = Arduino Uno (Rev3)
  LED1 = RGB LED (com. anode, rbg) [package="5 mm [THT]"]
  R1 = Resistor [tolerance=±5% resistance=220 package="1206 [SMD]"]
  R2 = Resistor [tolerance=±5% resistance=220 package="1206 [SMD]"]
  R3 = Resistor [tolerance=±5% resistance=220 package="2010 [SMD]"]
  R4 = Resistor [tolerance=±5% resistance=2.2k package="0603 [SMD]"]
  Part2 = Bluetooth HC-05 Macho
  R5 = Resistor [tolerance=±5% resistance=1k package="0603 [SMD]"]

nets:
  VCC: SparkFun_Load_Cell_Amplifier_-_HX1.VCC, Part1.VIN
  N1: SparkFun_Load_Cell_Amplifier_-_HX1.DAT, Part1.D4
  N2: SparkFun_Load_Cell_Amplifier_-_HX1.SCK, Part1.D5_PWM
  GND: SparkFun_Load_Cell_Amplifier_-_HX1.GND, Part1.GND, R4.Pin_0, Part2.GND
  N3: Part1.D9_PWM, R3.Pin_1
  N4: Part1.D10_PWM/SS, R1.Pin_1
  N5: Part1.D2, Part2.TXD
  N6: Part1.D3_PWM, R5.Pin_0
  N7: Part1.D6_PWM, R2.Pin_1
  5V: Part1.5V, LED1.common_anode, Part2.VCC
  N8: LED1.red_cathode, R2.Pin_0
  N9: LED1.blue_cathode, R3.Pin_0
  N10: LED1.green_cathode, R1.Pin_0
  N11: R4.Pin_1, Part2.RXD, R5.Pin_1

notes:
  ( A+ )
  PLANT LEAVE
  ( A– )
  PLANT SOIL

custom parts:
  SparkFun Load Cell Amplifier - HX711: The SparkFun Load Cell Amplifier is a small breakout board for the HX711 IC that allows you to easily read load cells to measure weight. By connecting the amplifier to your microcontroller you will be able to read the changes in the resistance of the load cell, and with some calibration you’ll be able to get very accurate weight measurements. This can be handy for creating your own industrial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
